# Fritzing sketch sketch (saved by Fritzing 0.9.3b)
breadboards: 1

parts:
  Componente1 = Arduino Mega ADK (Rev3)
  T1 = LM35 Temperature Sensor [package="TO92 [THT]"]
  LED1 = LED - 3mm [color="Red (633nm)" package="3 mm [THT]"]
  Q1 = TRANSISTOR_NPN [package=to-92]
  F1 = Fan - Ventilador [package=THT]
  LCD1 = LCD screen
  M3 = Stepper Motor - Bipolar
  Btn1 = Adafruit Push-button Power Switch Breakout [package=THT]
  Btn2 = Adafruit Push-button Power Switch Breakout [package=THT]
  Btn3 = Adafruit Push-button Power Switch Breakout [package=THT]
  Btn4 = Adafruit Push-button Power Switch Breakout [package=THT]
  LED2 = LED - 3mm [color="Red (633nm)" package="3 mm [THT]"]
  T2 = LM35 Temperature Sensor [package="TO92 [THT]"]
  Raspberry_Pi1 = Raspberry Pi B+  # not connected
  R1 = Resistor [tolerance=±5% resistance=220 package="0402 [SMD]"]
  R2 = Resistor [tolerance=±5% resistance=220 package="0402 [SMD]"]
  R3 = Resistor [tolerance=±5% resistance=220 package="0402 [SMD]"]
  S1 = H-Bridge with L298N

nets:
  N1: Componente1.A0, T2.Vout
  N2: Componente1.A1, T1.Vout
  N3: Componente1.D21/SCL, Btn3.IN
  N4: Componente1.D20/SDA, Btn4.IN
  N5: Componente1.D19/RX1, Btn1.IN
  N6: Componente1.D18/TX1, Btn2.IN
  N7: Componente1.D13_PWM, LCD1.DB7
  N8: Componente1.D12_PWM, LCD1.DB6
  N9: Componente1.D11_PWM, LCD1.DB5
  N10: Componente1.D10_PWM, LCD1.DB4
  N11: Componente1.D9_PWM, LCD1.E
  N12: Componente1.D8_PWM, LCD1.RS
  5V: Componente1.5V, T1.+Vs, Q1.E, LCD1.VDD, LCD1.R/W, LCD1.LED-, T2.+Vs
  GND: Componente1.GND, T1.GND, LCD1.VSS, LCD1.LED+, T2.GND, R2.Pin_0, R3.Pin_0, S1.GND
  N13: Componente1.D0/RX0, LED2.cathode
  N14: Componente1.D1/TX0, LED1.anode, R2.Pin_1
  N15: Componente1.D34, Q1.C
  N16: Componente1.D39, S1.IN1
  N17: Componente1.D41, S1.IN2
  N18: Componente1.D43, S1.IN3
  N19: Componente1.D45, S1.IN4
  N20: Q1.B, F1.5V
  GND_2: F1.GND, S1.12V
  N21: LCD1.V0, R1.Pin_1
  N22: M3.B, S1.OUT3-Motor2
  N23: M3.D, S1.OUT4-Motor2
  N24: LED2.anode, R3.Pin_1

custom parts:
  Fan - Ventilador: Ventilador de 2 pines, se encuentra comunmente en computadoras de escritorio
  LCD screen: A standard character display, usually with 2x16 characters. Comes in many colors.
  H-Bridge with L298N: h-bridge
